// Logisim project projeto de circuito 2.circ as structural Verilog: 4 circuits, main circuit main
module main (
  input  in_1,
  input  in_2,
  input  in_3,
  input  in_4,
  input  in_5,
  input  in_6,
  input  in_7,
  input  in_8,
  input  in_9,
  input  in_10,
  input  in_11,
  input  in_12
);

  wire numerouser_1_out_7, numerouseroeste_1_out_7;
  wire [3:0] numerouser_1_out_6, numerouseroeste_1_out_6, seletor_1_out_5, seletor_1_out_6;
  wire [4:0] numerouser_1_s, numerouseroeste_1_s;

  LED led_1 (.in(numerouser_1_out_7));
  Hex_Digit_Display hex_digit_display_1 (.value(numerouser_1_out_6));  // open: dp
  NumeroUser numerouser_1 (
    .out_7(numerouser_1_out_7), .out_6(numerouser_1_out_6), .in_1(in_3), .in_2(in_4), .in_3(in_5),
    .in_4(in_6), .in_5(in_7), .S(numerouser_1_s));
  Hex_Digit_Display hex_digit_display_2 (.value(seletor_1_out_5));  // open: dp
  Seletor seletor_1 (
    .in_1(in_1), .in_2(in_2), .in_3(numerouser_1_s), .in_4(numerouseroeste_1_s), .out_5(seletor_1_out_5),
    .out_6(seletor_1_out_6));
  Hex_Digit_Display hex_digit_display_3 (.value(seletor_1_out_6));  // open: dp
  LED led_2 (.in(numerouseroeste_1_out_7));
  Hex_Digit_Display hex_digit_display_4 (.value(numerouseroeste_1_out_6));  // open: dp
  NumeroUserOeste numerouseroeste_1 (
    .S(numerouseroeste_1_s), .out_7(numerouseroeste_1_out_7), .out_6(numerouseroeste_1_out_6), .in_1(in_8),
    .in_2(in_9), .in_3(in_10), .in_4(in_11), .in_5(in_12));

  // Notes on the sheet:
  //   Jogador A
  //   X
  //   Y
  //   Jogador B
endmodule

module NumeroUser (
  input  in_1,
  input  in_2,
  input  in_3,
  input  in_4,
  input  in_5,
  output [3:0] out_6,
  output out_7,
  output [4:0] S
);


  assign out_6 = {in_2, in_3, in_4, in_5};
  assign out_7 = in_1;
  assign S = {in_1, in_2, in_3, in_4, in_5};
endmodule

// NumeroUser
module NumeroUserOeste (
  input  in_1,
  input  in_2,
  input  in_3,
  input  in_4,
  input  in_5,
  output [3:0] out_6,
  output out_7,
  output [4:0] S
);


  assign out_6 = {in_2, in_3, in_4, in_5};
  assign out_7 = in_1;
  assign S = {in_1, in_2, in_3, in_4, in_5};
endmodule

module Seletor (
  input  in_1,
  input  in_2,
  input  [4:0] in_3,
  input  [4:0] in_4,
  output [3:0] out_5,
  output [3:0] out_6
);

  wire [4:0] multiplexer_1_out;
  wire [4:4] demultiplexer_1_out0, demultiplexer_1_out1;

  Demultiplexer #(.width(5), .enable("false")) demultiplexer_1 (
    .out0({demultiplexer_1_out0[4], out_5}), .out1({demultiplexer_1_out1[4], out_6}), .in(multiplexer_1_out),
    .sel(in_1));
  Multiplexer #(.width(5), .enable("false")) multiplexer_1 (
    .in0(in_3), .in1(in_4), .out(multiplexer_1_out), .sel(in_2));
endmodule
